// Logisim project S1-T2.circ as structural Verilog: 1 circuit, main circuit mainmodule
module mainmodule (
  input  [13:0] ENTRY_VEHICLE_WEIGHT,
  input  [13:0] EXIT_VEHICLE_WEIGHT,
  output [7:0] TOTAL_CARS_ENTERED,
  output [7:0] TOTAL_CARS_PRESENT_IN_PARKING_LOT,
  output [7:0] TOTAL_BIKES_ENTERED,
  output [7:0] TOTAL_BIKES_PRESENT_IN_PARKING_LOT
);

  wire and_1_out, and_2_out, and_3_out, and_4_out, button_1_out, button_2_out, button_3_out, button_4_out,
       button_5_out, button_6_out, button_7_out, button_8_out, comparator_1_eq, comparator_2_eq,
       comparator_3_eq, comparator_3_gt, comparator_3_lt, comparator_4_eq, comparator_5_eq, comparator_6_eq,
       comparator_6_gt, comparator_6_lt, or_1_out, or_2_out, or_3_out, or_4_out, or_5_out, or_6_out;
  wire [1:0] counter_1_q, counter_4_q;
  wire [7:0] adder_1_out, adder_2_out, counter_5_q, counter_6_q, multiplexer_1_out, multiplexer_2_out;

  Button button_1 (.out(button_1_out));
  Button button_2 (.out(button_2_out));
  Button button_3 (.out(button_3_out));
  Button button_4 (.out(button_4_out));
  or or_1 (or_1_out, button_1_out, button_3_out);
  or or_2 (or_2_out, button_4_out, button_2_out);
  Adder adder_1 (.a(TOTAL_BIKES_ENTERED), .b(8'h2), .out(adder_1_out));  // open: cin, cout
  Counter #(.width(2), .max('h3)) counter_1 (
    .Q(counter_1_q), .clk(or_1_out), .clr(or_2_out));  // open: load, D, count, carry
  Comparator #(.width(2)) comparator_1 (.a(2'b01), .b(counter_1_q), .eq(comparator_1_eq));  // open: gt, lt
  Comparator #(.width(2)) comparator_2 (.a(counter_1_q), .b(2'b10), .eq(comparator_2_eq));  // open: gt, lt
  Comparator #(.width(14)) comparator_3 (
    .a(ENTRY_VEHICLE_WEIGHT), .b(14'h400), .gt(comparator_3_gt), .eq(comparator_3_eq), .lt(comparator_3_lt));
  Multiplexer #(.width(8), .enable("false")) multiplexer_1 (
    .in0(TOTAL_BIKES_ENTERED), .in1(adder_1_out), .out(multiplexer_1_out), .sel(comparator_3_lt));
  or or_3 (or_3_out, comparator_3_gt, comparator_3_eq);
  and and_1 (and_1_out, comparator_3_lt, comparator_2_eq);
  and and_2 (and_2_out, comparator_2_eq, or_3_out);
  Counter counter_2 (
    .load(and_1_out), .D(multiplexer_1_out), .count(comparator_1_eq), .Q(TOTAL_BIKES_ENTERED), .clk(or_2_out));  // open: carry, clr
  Counter counter_3 (.count(and_2_out), .Q(TOTAL_CARS_ENTERED), .clk(or_2_out));  // open: load, D, carry, clr
  Subtractor subtractor_1 (
    .a(TOTAL_BIKES_ENTERED), .b(counter_5_q), .out(TOTAL_BIKES_PRESENT_IN_PARKING_LOT));  // open: bin, bout
  Subtractor subtractor_2 (
    .a(TOTAL_CARS_ENTERED), .b(counter_6_q), .out(TOTAL_CARS_PRESENT_IN_PARKING_LOT));  // open: bin, bout
  or or_4 (or_4_out, button_5_out, button_6_out);
  Adder adder_2 (.a(counter_5_q), .b(8'h2), .out(adder_2_out));  // open: cin, cout
  Counter #(.width(2), .max('h3)) counter_4 (
    .Q(counter_4_q), .clk(or_4_out), .clr(or_6_out));  // open: load, D, count, carry
  Comparator #(.width(2)) comparator_4 (.a(2'b01), .b(counter_4_q), .eq(comparator_4_eq));  // open: gt, lt
  Comparator #(.width(2)) comparator_5 (.a(counter_4_q), .b(2'b10), .eq(comparator_5_eq));  // open: gt, lt
  Comparator #(.width(14)) comparator_6 (
    .a(EXIT_VEHICLE_WEIGHT), .b(14'h400), .gt(comparator_6_gt), .eq(comparator_6_eq), .lt(comparator_6_lt));
  Multiplexer #(.width(8), .enable("false")) multiplexer_2 (
    .in0(counter_5_q), .in1(adder_2_out), .out(multiplexer_2_out), .sel(comparator_6_lt));
  or or_5 (or_5_out, comparator_6_gt, comparator_6_eq);
  and and_3 (and_3_out, comparator_6_lt, comparator_5_eq);
  Counter counter_5 (
    .load(and_3_out), .D(multiplexer_2_out), .count(comparator_4_eq), .Q(counter_5_q), .clk(or_6_out));  // open: carry, clr
  Counter counter_6 (.count(and_4_out), .Q(counter_6_q), .clk(or_6_out));  // open: load, D, carry, clr
  and and_4 (and_4_out, comparator_5_eq, or_5_out);
  or or_6 (or_6_out, button_7_out, button_8_out);
  Button button_5 (.out(button_5_out));
  Button button_6 (.out(button_6_out));
  Button button_7 (.out(button_7_out));
  Button button_8 (.out(button_8_out));

  // Notes on the sheet:
  //   ENTRY
  //   EXIT
endmodule
